# Fritzing sketch TMWL (saved by Fritzing 1.0.5)
breadboards: 1

parts:
  Part1 = Arduino Uno (Rev3)
  C1 = Electrolytic Capacitor [capacitance=4.7mF voltage=35V package="1010 [SMD, electrolytic]"]
  C2 = Electrolytic Capacitor [capacitance=4.7mF voltage=35V package="1010 [SMD, electrolytic]"]
  C3 = Electrolytic Capacitor [capacitance=4.7mF voltage=35V package="1010 [SMD, electrolytic]"]
  C4 = Electrolytic Capacitor [capacitance=4.7mF voltage=35V package="1010 [SMD, electrolytic]"]
  C5 = Electrolytic Capacitor [capacitance=4.7mF voltage=35V package="1010 [SMD, electrolytic]"]
  C6 = Electrolytic Capacitor [capacitance=4.7mF voltage=35V package="1010 [SMD, electrolytic]"]
  C7 = Electrolytic Capacitor [capacitance=4.7mF voltage=35V package="1010 [SMD, electrolytic]"]
  C8 = Electrolytic Capacitor [capacitance=4.7mF voltage=35V package="1010 [SMD, electrolytic]"]
  Servo_8 = Basic Servo
  Servo_7 = Basic Servo
  Servo_6 = Basic Servo
  Servo_5 = Basic Servo
  Servo_4 = Basic Servo
  Servo_3 = Basic Servo
  Servo_2 = Basic Servo
  Servo_1 = Basic Servo
  Distractor_Servo_1 = Basic Servo
  C9 = Electrolytic Capacitor [capacitance=4.7mF voltage=35V package="1010 [SMD, electrolytic]"]
  C10 = Electrolytic Capacitor [capacitance=4.7mF voltage=35V package="1010 [SMD, electrolytic]"]
  Distractor_Servo_2 = Basic Servo
  YwRobot_Power_Supply2 = YwRobot Breadboard Power Supply [part_number=545043]
  PC_Connection = USB A Plug  # not connected

nets:
  N1: Part1.D8, Servo_6.pulse
  N2: Part1.D9_PWM, Servo_7.pulse
  N3: Part1.D10_PWM/SS, Servo_3.pulse
  N4: Part1.D11_PWM/MOSI, Servo_8.pulse
  N5: Part1.D12/MISO, Servo_4.pulse
  GND: Part1.GND, Servo_8.gnd, Servo_7.gnd, Servo_6.gnd, Servo_5.gnd, Servo_4.gnd, Servo_3.gnd, Servo_2.gnd, Servo_1.gnd, Distractor_Servo_1.gnd, Distractor_Servo_2.gnd, YwRobot_Power_Supply2.GND
  N6: Part1.D2, Distractor_Servo_1.pulse
  N7: Part1.D3_PWM, Distractor_Servo_2.pulse
  N8: Part1.D5_PWM, Servo_5.pulse
  N9: Part1.D6_PWM, Servo_1.pulse
  N10: Part1.D7, Servo_2.pulse
  VCC: C1.-, C1.+, C3.-, C3.+, C6.-, C6.+, C8.-, C8.+, Servo_8.vcc, Servo_7.vcc, Servo_6.vcc, Servo_5.vcc, Distractor_Servo_1.vcc, C10.-, C10.+, YwRobot_Power_Supply2.VCC#9
  VCC_2: C2.-, C2.+, C4.-, C4.+, C5.-, C5.+, C7.-, C7.+, Servo_4.vcc, Servo_3.vcc, Servo_2.vcc, Servo_1.vcc, C9.-, C9.+, Distractor_Servo_2.vcc, YwRobot_Power_Supply2.VCC#5

notes:
  Servo Power supply

custom parts:
  YwRobot Breadboard Power Supply: The YwRobot Breadboard Power Supply (MB-V2) has two power rails; they can be 5V or 3V3. Power to the module can be provided through the female USB socket or through the A10 (female) 2.1mm power jack.

// code stored in the sketch: TMWL.ino
#include "Servo.h"  

Servo servo1; 
Servo servo2;
Servo servo3;
Servo servo4;
Servo servo5;
Servo servo6;
Servo servo7;
Servo servo8;

Servo servoMask1;
Servo servoMask2;

int firstServo = 0;
int secondServo = 0;
int lastServo = 0;
int palpationTime = 6000;
unsigned long timer = 0;
unsigned long mask1Timer = 0;
unsigned long mask2Timer = 0;
bool runTask = false;
bool runDemo = false;
int angle = 0;
int multiplier = 1;

bool servosReset = false;

void setup()
{
  Serial.begin(9600); 
  
  servo1.attach(6);  
  servo2.attach(7);
  servo3.attach(10);
  servo4.attach(12);
  servo5.attach(5);
  servo6.attach(8);
  servo7.attach(9);
  servo8.attach(11);

  servoMask1.attach(3);
  servoMask2.attach(2);
}

void loop()
{ 
  switch (Serial.read()) {
    case 'S':
      runTask = true;
      break;
    case 'O':
      runTask = false;
      runDemo = false;
      break;
    case 'D':
      runDemo = true;
      break;
  }

  if(!runDemo && !runTask && !servosReset) {
      servo1.write(110); 
      servo2.write(90);
      servo3.write(80);
      servo4.write(80);
      servo5.write(90);
      servo6.write(90);
      servo7.write(90);
      servo8.write(90);

      servosReset = true;
  }

  if (runDemo) {
    servosReset = false;
    servo1.write(60); 
    servo2.write(60);    
    servo3.write(130);    
    servo4.write(130);    
    servo5.write(60);    
    servo6.write(50);   
    servo7.write(60);   
    servo8.write(60);
  }
  
  if(runTask) {
    servosReset = false;
    if(millis() - mask1Timer > 3200) {
        mask1Timer = millis();
        angle =  multiplier*30 + angle;
        if(angle >= 180) {
          multiplier = -1;
          angle = 180;
        }
        else if(angle <= 0) {
          multiplier = 1;
          angle = 0;
        }
        servoMask1.write(angle);
      }

    if(millis() - mask2Timer > 4500) {
        mask2Timer = millis();
        angle =  multiplier*30 + angle;
        if(angle >= 180) {
          multiplier = -1;
          angle = 180;
        }
        else if(angle <= 0) {
          multiplier = 1;
          angle = 0;
        }
        servoMask2.write(angle);
      }
    
    if(millis() - timer > palpationTime/2) {
      timer = millis();
      lastServo = secondServo;
      secondServo = firstServo;
      while(lastServo == firstServo || secondServo == firstServo) {
        firstServo = random(1,9);
      } 

      if(secondServo != 1) {
        servo1.write(110); 
      }
      if(secondServo != 2) {
        servo2.write(90);
      }
      if(secondServo != 3) {
        servo3.write(80);
      }
      if(secondServo != 4) {
        servo4.write(80);
      }
      if(secondServo != 5) {
        servo5.write(90);
      }
      if(secondServo != 6) {
        servo6.write(90);
      }
      if(secondServo != 7) {
        servo7.write(90);
      }
      if(secondServo != 8) {
        servo8.write(90);
      }

      while (millis()-timer < 1000) {}
      Serial.println(String(firstServo));

      if(firstServo==1) {
        servo1.write(60); 
      }
      else if(firstServo == 2) {
        servo2.write(60);
      }
      else if(firstServo == 3) {
        servo3.write(130);
      }
      else if(firstServo == 4) {
        servo4.write(130);
      }
      else if(firstServo == 5) {
        servo5.write(60);
      }
      else if(firstServo == 6) {
        servo6.write(50);
      }
      else if(firstServo == 7) {
        servo7.write(50);
      }
      else if(firstServo == 8) {
        servo8.write(60);
      }
      timer = millis();
    } 
  }
}

// code stored in the sketch: tmwl_primTask.ino
#include "Servo.h"  

Servo servo1; 
Servo servo2;
Servo servo3;
Servo servo4;
Servo servo5;
Servo servo6;
Servo servo7;
Servo servo8;

Servo servoMask1;
Servo servoMask2;

int firstServo = 0;
int secondServo = 0;
int lastServo = 0;
int palpationTime = 6000;
unsigned long timer = 0;
unsigned long mask1Timer = 0;
unsigned long mask2Timer = 0;
bool runTask = false;
bool runDemo = false;
int angle = 0;
int multiplier = 1;

bool servosReset = false;

void setup()
{
  Serial.begin(9600); 
  
  servo1.attach(6);  
  servo2.attach(7);
  servo3.attach(10);
  servo4.attach(12);
  servo5.attach(5);
  servo6.attach(8);
  servo7.attach(9);
  servo8.attach(11);

  servoMask1.attach(3);
  servoMask2.attach(2);
}

void loop()
{ 
  switch (Serial.read()) {
    case 'S':
      runTask = true;
      break;
    case 'O':
      runTask = false;
      runDemo = false;
      break;
    case 'D':
      runDemo = true;
      break;
  }

  if(!runDemo && !runTask && !servosReset) {
      servo1.write(110); 
      servo2.write(90);
      servo3.write(80);
      servo4.write(80);
      servo5.write(90);
      servo6.write(90);
      servo7.write(90);
      servo8.write(90);

      servosReset = true;
  }

  if (runDemo) {
    servosReset = false;
    servo1.write(60); 
    servo2.write(60);    
    servo3.write(130);    
    servo4.write(130);    
    servo5.write(60);    
    servo6.write(50);   
    servo7.write(60);   
    servo8.write(60);
  }
  
  if(runTask) {
    servosReset = false;
    if(millis() - mask1Timer > 3200) {
        mask1Timer = millis();
        angle =  multiplier*30 + angle;
        if(angle >= 180) {
          multiplier = -1;
          angle = 180;
        }
        else if(angle <= 0) {
          multiplier = 1;
          angle = 0;
        }
        servoMask1.write(angle);
      }

    if(millis() - mask2Timer > 4500) {
        mask2Timer = millis();
        angle =  multiplier*30 + angle;
        if(angle >= 180) {
          multiplier = -1;
          angle = 180;
        }
        else if(angle <= 0) {
          multiplier = 1;
          angle = 0;
        }
        servoMask2.write(angle);
      }
    
    if(millis() - timer > palpationTime/2) {
      timer = millis();
      lastServo = secondServo;
      secondServo = firstServo;
      while(lastServo == firstServo || secondServo == firstServo) {
        firstServo = random(1,9);
      } 

      if(secondServo != 1) {
        servo1.write(110); 
      }
      if(secondServo != 2) {
        servo2.write(90);
      }
      if(secondServo != 3) {
        servo3.write(80);
      }
      if(secondServo != 4) {
        servo4.write(80);
      }
      if(secondServo != 5) {
        servo5.write(90);
      }
      if(secondServo != 6) {
        servo6.write(90);
      }
      if(secondServo != 7) {
        servo7.write(90);
      }
      if(secondServo != 8) {
        servo8.write(90);
      }

      while (millis()-timer < 1000) {}
      Serial.println(String(firstServo));

      if(firstServo==1) {
        servo1.write(60); 
      }
      else if(firstServo == 2) {
        servo2.write(60);
      }
      else if(firstServo == 3) {
        servo3.write(130);
      }
      else if(firstServo == 4) {
        servo4.write(130);
      }
      else if(firstServo == 5) {
        servo5.write(60);
      }
      else if(firstServo == 6) {
        servo6.write(50);
      }
      else if(firstServo == 7) {
        servo7.write(50);
      }
      else if(firstServo == 8) {
        servo8.write(60);
      }
      timer = millis();
    } 
  }
}
